# Fritzing sketch ControlPanel (saved by Fritzing 0.9.2b)
circuit board: 8.46667cm x 5.64444cm
breadboards: 1

parts:
  Raspberry_Pi_3 = Raspberry Pi 3
  S1 = Toggle Switch [package=THT]
  S2 = Toggle Switch [package=THT]
  S3 = Toggle Switch [package=THT]
  R1 = Resistor [tolerance=±5% resistance=220 package=THT]
  R2 = Resistor [tolerance=±5% resistance=220 package=THT]
  R3 = Resistor [tolerance=±5% resistance=220 package=THT]
  U1 = LCD-16X2 [package=lcd-16x2]
  R4 = Trimmer Potentiometer [maximum_resistance=10kΩ package=THT]
  R5 = Resistor [tolerance=±5% resistance=220 package=THT]

nets:
  3V3: Raspberry_Pi_3.3v3, Raspberry_Pi_3.3V3, S1.COM, S2.COM, S3.COM, U1.VDD, R4.leg1, R5.Pin_1
  N1: Raspberry_Pi_3.GIPO17, U1.DB5
  N2: Raspberry_Pi_3.GIPO19, U1.DB7
  N3: Raspberry_Pi_3.GIPO26, U1.DB4
  GND: Raspberry_Pi_3.GND, U1.VSS, U1.R_W, U1.K, R4.wiper
  N4: Raspberry_Pi_3.GIPO21, U1.DB6
  N5: Raspberry_Pi_3.GIPO16, U1.E
  N6: Raspberry_Pi_3.GIPO12, U1.RS
  N7: Raspberry_Pi_3.GIPO25, R1.Pin_0
  N8: Raspberry_Pi_3.GIPO24, R2.Pin_0
  N9: Raspberry_Pi_3.GIPO23, R3.Pin_0
  N10: S1.L2, R1.Pin_1
  N11: S2.L2, R2.Pin_1
  N12: S3.L2, R3.Pin_1
  N13: U1.VO, R4.leg2
  N14: U1.A, R5.Pin_0
