# Fritzing sketch fanchicken (saved by Fritzing 0.9.0b)
circuit board: 8.46667cm x 5.64444cm
breadboards: 1

parts:
  R1 = Resistor [tolerance=±5% resistance=4.7k package=THT]
  R2 = Resistor [tolerance=±5% resistance=4.7k package=THT]
  S1 = Toggle Switch [package=THT]
  S2 = Toggle Switch [package=THT]
  Part2 = Arduino Micro (Rev3)
  U1 = RELAY-2 [package=relay-g5v]
  M1 = DC Motor
  M2 = DC Motor
  M3 = DC Motor
  fanPowerSource = Screw terminal - 2 pins [package=THT]

nets:
  N1: R1.Pin_0, R2.Pin_0, Part2.GND, U1.9
  N2: R1.Pin_1, S2.COM, Part2.D12_PWM/A11
  N3: R2.Pin_1, S1.COM, Part2.D11_PWM
  N4: S1.L2, S2.L2, Part2.5V
  N5: Part2.D8_PWM/A8, U1.2
  N6: U1.1, M1.pin_1, M2.pin_1, M3.pin_1
  N7: U1.10, fanPowerSource.pin1
  N8: M1.pin_2, M2.pin_2, M3.pin_2, fanPowerSource.pin2
